# Fritzing sketch minitankbot (saved by Fritzing 0.9.2b)
breadboards: 1

parts:
  Part1 = Arduino Ethernet Shield (Rev3)  # not connected
  S1 = Pushbutton [package="[THT]"]
  Part2 = 3-Axis Accelerometer Breakout - MMA8452Q  # not connected

nets:
  N1: S1.Pin_1, S1.Pin_2
  N2: S1.Pin_3, S1.Pin_4
